// Logisim project Task 1.1 Implementations of NOT gate using NAND gate.circ as structural Verilog: 1 circuit, main circuit main
module main (
  input  A,
  output Y
);

  nand nand_1 (Y, A, A);

  // Notes on the sheet:
  //   Fig: Implementation of NOT gate using NAND gate
endmodule
