// Logisim project Task 1.2 Implementations of And gate using NAND gates.circ as structural Verilog: 1 circuit, main circuit main
module main (
  input  A,
  input  B,
  output Y
);

  wire nand_1_out;

  nand nand_1 (nand_1_out, A, B);
  nand nand_2 (Y, nand_1_out, nand_1_out);

  // Notes on the sheet:
  //   Fig: Implementation of AND gate using NAND gates
endmodule
