// Logisim project Task 1.4 Implementations of NOT gate using NOR gate.circ as structural Verilog: 1 circuit, main circuit main
module main (
  input  A,
  output Y
);

  nor nor_1 (Y, A, A);

  // Notes on the sheet:
  //   Fig: Implementation of NOT gate using NOR gate
endmodule
