// Logisim project Task 1.5 Implementations of And gate using NOR gates.circ as structural Verilog: 1 circuit, main circuit main
module main (
  input  A,
  input  B,
  output Y
);

  wire nor_1_out, nor_2_out;

  nor nor_1 (nor_1_out, A, A);
  nor nor_2 (nor_2_out, B, B);
  nor nor_3 (Y, nor_1_out, nor_2_out);

  // Notes on the sheet:
  //   Fig: Implementation of AND gate using NOR gates
endmodule
