// Logisim project Task 1.6 Implementations of OR gate using NOR gates.circ as structural Verilog: 1 circuit, main circuit main
module main (
  input  A,
  input  B,
  output Y
);

  wire nor_1_out;

  nor nor_1 (nor_1_out, A, B);
  nor nor_2 (Y, nor_1_out, nor_1_out);

  // Notes on the sheet:
  //   Fig: Implementation of OR gate using NOR gates
endmodule
