// Logisim project Task 2.2 Implementations of XNOR gate using NAND gates.circ as structural Verilog: 1 circuit, main circuit main
module main (
  input  A,
  input  B,
  output Y
);

  wire nand_1_out, nand_2_out, nand_3_out, nand_4_out;

  nand nand_1 (nand_1_out, A, B);
  nand nand_2 (nand_2_out, A, nand_1_out);
  nand nand_3 (nand_3_out, nand_1_out, B);
  nand nand_4 (nand_4_out, nand_2_out, nand_3_out);
  nand nand_5 (Y, nand_4_out, nand_4_out);

  // Notes on the sheet:
  //   Fig: Implementation of XNOR gate using NAND gates
endmodule
