// Logisim project Task 3.1 IC - Universal (NAND) gate implementation of the circuit - AC+BC'.circ as structural Verilog: 2 circuits, main circuit main
module main (
  input  A,
  input  B,
  input  C,
  output Y
);

  wire n7400_nand_1__3, n7400_nand_1__6, n7400_nand_1__8;

  _7400_NAND u_7400_nand_1 (
    ._1(A), ._2(C), ._4(C), ._5(C), ._9(n7400_nand_1__6), ._10(B), ._12(n7400_nand_1__8),
    ._13(n7400_nand_1__3), ._3(n7400_nand_1__3), ._6(n7400_nand_1__6), ._8(n7400_nand_1__8), ._11(Y));

  // Notes on the sheet:
  //   Fig: IC - Universal (NAND) gate implementation of the circuit - AC+BC'
endmodule

module _7400_NAND (
  input  _1,
  input  _2,
  input  _4,
  input  _5,
  input  _9,
  input  _10,
  input  _12,
  input  _13,
  output _3,
  output _6,
  output _8,
  output _11
);

  nand nand_1 (_3, _1, _2);
  nand nand_2 (_6, _4, _5);
  nand nand_3 (_8, _9, _10);
  nand nand_4 (_11, _12, _13);
endmodule
