// Logisim project Task 3.2 IC - Universal (NOR) gate implementation of the circuit - AC+BC'.circ as structural Verilog: 2 circuits, main circuit main
module main (
  input  A,
  input  B,
  input  C,
  output Y
);

  wire n7402_nor_1__1, n7402_nor_1__4, n7402_nor_1__10, n7402_nor_1__13, n7402_nor_2__1, n7402_nor_2__4;

  _7402_NOR u_7402_nor_1 (
    ._2(A), ._3(A), ._5(C), ._6(C), ._8(n7402_nor_1__4), ._9(n7402_nor_1__1), ._11(n7402_nor_1__10),
    ._12(n7402_nor_2__4), ._1(n7402_nor_1__1), ._4(n7402_nor_1__4), ._10(n7402_nor_1__10),
    ._13(n7402_nor_1__13));
  _7402_NOR u_7402_nor_2 (
    ._2(B), ._3(B), ._5(n7402_nor_2__1), ._6(C), ._11(n7402_nor_1__13), ._12(n7402_nor_1__13),
    ._1(n7402_nor_2__1), ._4(n7402_nor_2__4), ._13(Y));  // open: _8, _9, _10

  // Notes on the sheet:
  //   Fig: IC - Universal (NOR) gate implementation of the circuit - AC+BC'
endmodule

module _7402_NOR (
  input  _2,
  input  _3,
  input  _5,
  input  _6,
  input  _8,
  input  _9,
  input  _11,
  input  _12,
  output _1,
  output _4,
  output _10,
  output _13
);

  nor nor_1 (_1, _2, _3);
  nor nor_2 (_4, _5, _6);
  nor nor_3 (_10, _8, _9);
  nor nor_4 (_13, _11, _12);
endmodule
