// Logisim project 1st Canonical Form.circ as structural Verilog: 1 circuit, main circuit main
module main (
  input  A,
  input  B,
  input  C,
  output F__SOP
);

  wire and_1_out, and_2_out, and_3_out, not_1_out, not_2_out, not_3_out;

  not not_1 (not_1_out, B);
  not not_2 (not_2_out, A);
  not not_3 (not_3_out, C);
  and and_1 (and_1_out, not_2_out, not_1_out, C);
  and and_2 (and_2_out, not_2_out, B, not_3_out);
  and and_3 (and_3_out, A, B, not_3_out);
  or or_1 (F__SOP, and_1_out, and_2_out, and_3_out);
endmodule
