// Logisim project 2nd Canonical Form.circ as structural Verilog: 1 circuit, main circuit main
module main (
  input  A,
  input  B,
  input  C,
  output F__POS
);

  wire and_1_out, not_1_out, not_2_out, not_3_out, or_1_out, or_2_out, or_3_out, or_4_out, or_5_out,
       or_6_out, or_7_out;

  not not_1 (not_1_out, B);
  not not_2 (not_2_out, A);
  not not_3 (not_3_out, C);
  or or_1 (or_1_out, A, B, C);
  or or_2 (or_2_out, A, not_1_out, not_3_out);
  or or_3 (or_3_out, not_2_out, B, C);
  or or_4 (or_4_out, not_2_out, B);
  or or_5 (or_5_out, not_2_out, not_1_out);
  and and_1 (and_1_out, or_1_out, or_2_out, or_3_out);
  or or_6 (or_6_out, or_4_out, not_3_out);
  or or_7 (or_7_out, or_5_out, not_3_out);
  and and_2 (F__POS, and_1_out, or_6_out, or_7_out);
endmodule
