// Logisim project IC - 2nd Canonical Form.circ as structural Verilog: 4 circuits, main circuit main
module main (
  input  A,
  input  B,
  input  C,
  output F
);

  wire n4075_3_input_or_1__6, n4075_3_input_or_1__9, n4075_3_input_or_1__10, n4075_3_input_or_2__9,
       n4075_3_input_or_2__10, n7404_hex_inverters_1__2, n7404_hex_inverters_1__4, n7404_hex_inverters_1__6,
       n7411_3_input_and_1__12;

  _7404_Hex_Inverters u_7404_hex_inverters_1 (
    ._1(A), ._3(B), ._5(C), ._2(n7404_hex_inverters_1__2), ._4(n7404_hex_inverters_1__4),
    ._6(n7404_hex_inverters_1__6));  // open: _9, _11, _13, _8, _10, _12
  _4075_3_input_OR u_4075_3_input_or_1 (
    ._1(A), ._2(B), ._8(C), ._3(A), ._4(n7404_hex_inverters_1__4), ._5(n7404_hex_inverters_1__6), ._11(C),
    ._12(B), ._13(n7404_hex_inverters_1__2), ._9(n4075_3_input_or_1__9), ._6(n4075_3_input_or_1__6),
    ._10(n4075_3_input_or_1__10));
  _4075_3_input_OR u_4075_3_input_or_2 (
    ._1(n7404_hex_inverters_1__2), ._2(B), ._8(n7404_hex_inverters_1__6), ._11(n7404_hex_inverters_1__2),
    ._12(n7404_hex_inverters_1__4), ._13(n7404_hex_inverters_1__6), ._9(n4075_3_input_or_2__9),
    ._10(n4075_3_input_or_2__10));  // open: _3, _4, _5, _6
  _7411_3_input_AND u_7411_3_input_and_1 (
    ._1(n4075_3_input_or_1__9), ._2(n4075_3_input_or_1__6), ._13(n4075_3_input_or_1__10),
    ._3(n7411_3_input_and_1__12), ._4(n4075_3_input_or_2__10), ._5(n4075_3_input_or_2__9),
    ._12(n7411_3_input_and_1__12), ._6(F));  // open: _9, _10, _11, _8

  // Notes on the sheet:
  //   Fig: 2nd Canonical Form (F=(A+B+C)(A+B'+C')(A'+B+C)(A'+B+C')(A'+B'+C'))
endmodule

module _7404_Hex_Inverters (
  input  _1,
  input  _3,
  input  _5,
  input  _9,
  input  _11,
  input  _13,
  output _2,
  output _4,
  output _6,
  output _8,
  output _10,
  output _12
);

  not not_1 (_2, _1);
  not not_2 (_4, _3);
  not not_3 (_6, _5);
  not not_4 (_8, _9);
  not not_5 (_10, _11);
  not not_6 (_12, _13);
endmodule

module _7411_3_input_AND (
  input  _1,
  input  _2,
  input  _13,
  input  _3,
  input  _4,
  input  _5,
  input  _9,
  input  _10,
  input  _11,
  output _12,
  output _6,
  output _8
);

  and and_1 (_12, _1, _2, _13);
  and and_2 (_6, _3, _4, _5);
  and and_3 (_8, _9, _10, _11);
endmodule

module _4075_3_input_OR (
  input  _1,
  input  _2,
  input  _8,
  input  _3,
  input  _4,
  input  _5,
  input  _11,
  input  _12,
  input  _13,
  output _9,
  output _6,
  output _10
);

  or or_1 (_9, _1, _2, _8);
  or or_2 (_6, _3, _4, _5);
  or or_3 (_10, _11, _12, _13);
endmodule
