// Logisim project BCD to Excess-3 Converter.circ as structural Verilog: 1 circuit, main circuit main
module main (
  input  W,
  input  X,
  input  Y,
  input  Z,
  output A,
  output B,
  output C,
  output D
);

  wire and_1_out, and_2_out, and_3_out, and_4_out, and_5_out, and_6_out, and_7_out, not_1_out, not_3_out;

  not not_1 (not_1_out, X);
  // NOT_Gate not_2 has open pins: in=W, out=open
  not not_3 (not_3_out, Y);
  not not_4 (D, Z);
  and and_1 (and_1_out, X, Y);
  and and_2 (and_2_out, X, Z);
  and and_3 (and_3_out, not_1_out, Y);
  and and_4 (and_4_out, not_1_out, Z);
  and and_5 (and_5_out, X, not_3_out, D);
  and and_6 (and_6_out, Y, Z);
  and and_7 (and_7_out, not_3_out, D);
  or or_1 (A, W, and_1_out, and_2_out);
  or or_2 (B, and_3_out, and_4_out, and_5_out);
  or or_3 (C, and_6_out, and_7_out);

  // Notes on the sheet:
  //   Fig: BCD to Excess-3 Converter
  //   =W+XY+XZ
  //   =X'Y+X'Z+XY'Z'
  //   =YZ+Y'Z'
  //   =Z'
endmodule
