// Logisim project IC - BCD to Excess-3 Converter.circ as structural Verilog: 5 circuits, main circuit main
module main (
  input  W,
  input  X,
  input  Y,
  input  Z,
  output A,
  output B,
  output C,
  output D
);

  wire n7404_hex_inverters_1__2, n7404_hex_inverters_1__4, n7408_quad_2_input_and_1__3,
       n7408_quad_2_input_and_1__6, n7408_quad_2_input_and_1__8, n7408_quad_2_input_and_1__11,
       n7408_quad_2_input_and_2__3, n7408_quad_2_input_and_2__6, n7411_triple_3_input_and_1__12;

  _7404_Hex_Inverters u_7404_hex_inverters_1 (
    ._1(X), ._3(Y), ._5(Z), ._2(n7404_hex_inverters_1__2), ._4(n7404_hex_inverters_1__4), ._6(D));  // open: _9, _11, _13, _8, _10, _12
  _7408_Quad_2_input_AND_Gate u_7408_quad_2_input_and_1 (
    ._1(X), ._2(Y), ._4(X), ._5(Z), ._9(n7404_hex_inverters_1__2), ._10(Y), ._12(n7404_hex_inverters_1__2),
    ._13(Z), ._3(n7408_quad_2_input_and_1__3), ._6(n7408_quad_2_input_and_1__6),
    ._8(n7408_quad_2_input_and_1__8), ._11(n7408_quad_2_input_and_1__11));
  _7411_Triple_3_input_AND u_7411_triple_3_input_and_1 (
    ._1(X), ._2(n7404_hex_inverters_1__4), ._13(D), ._12(n7411_triple_3_input_and_1__12));  // open: _3, _4, _5, _9, _10, _11, _6, _8
  _7408_Quad_2_input_AND_Gate u_7408_quad_2_input_and_2 (
    ._1(Y), ._2(Z), ._4(n7404_hex_inverters_1__4), ._5(D), ._3(n7408_quad_2_input_and_2__3),
    ._6(n7408_quad_2_input_and_2__6));  // open: _9, _10, _12, _13, _8, _11
  _4075_Triple_3_input_OR u_4075_triple_3_input_or_1 (
    ._1(W), ._2(n7408_quad_2_input_and_1__3), ._8(n7408_quad_2_input_and_1__6),
    ._3(n7408_quad_2_input_and_1__8), ._4(n7408_quad_2_input_and_1__11), ._5(n7411_triple_3_input_and_1__12),
    ._11(n7408_quad_2_input_and_2__3), ._12(n7408_quad_2_input_and_2__6), ._13(n7408_quad_2_input_and_2__6),
    ._9(A), ._6(B), ._10(C));

  // Notes on the sheet:
  //   Fig: BCD to Excess-3 Converter
  //   A=W+XY+XZ
  //   C=YZ+Y'Z'
  //   B=X'Y+X'Z+XY'Z'
  //   D=Z'
endmodule

module _7404_Hex_Inverters (
  input  _1,
  input  _3,
  input  _5,
  input  _9,
  input  _11,
  input  _13,
  output _2,
  output _4,
  output _6,
  output _8,
  output _10,
  output _12
);

  not not_1 (_2, _1);
  not not_2 (_4, _3);
  not not_3 (_6, _5);
  not not_4 (_8, _9);
  not not_5 (_10, _11);
  not not_6 (_12, _13);
endmodule

module _7411_Triple_3_input_AND (
  input  _1,
  input  _2,
  input  _13,
  input  _3,
  input  _4,
  input  _5,
  input  _9,
  input  _10,
  input  _11,
  output _12,
  output _6,
  output _8
);

  and and_1 (_12, _1, _2, _13);
  and and_2 (_6, _3, _4, _5);
  and and_3 (_8, _9, _10, _11);
endmodule

module _4075_Triple_3_input_OR (
  input  _1,
  input  _2,
  input  _8,
  input  _3,
  input  _4,
  input  _5,
  input  _11,
  input  _12,
  input  _13,
  output _9,
  output _6,
  output _10
);

  or or_1 (_9, _1, _2, _8);
  or or_2 (_6, _3, _4, _5);
  or or_3 (_10, _11, _12, _13);
endmodule

module _7408_Quad_2_input_AND_Gate (
  input  _1,
  input  _2,
  input  _4,
  input  _5,
  input  _9,
  input  _10,
  input  _12,
  input  _13,
  output _3,
  output _6,
  output _8,
  output _11
);

  and and_1 (_3, _1, _2);
  and and_2 (_6, _4, _5);
  and and_3 (_8, _9, _10);
  and and_4 (_11, _12, _13);
endmodule
