// Logisim project 2-bit Adder-Subtractor.circ as structural Verilog: 1 circuit, main circuit main
module main (
  input  CIN,
  input  A1,
  input  B1,
  input  A2,
  input  B2,
  output [1:0] A2_A1,
  output [1:0] S2_S1,
  output [1:0] B2_B1,
  output COUT
);

  wire adder_1_cout, xor_1_out, xor_2_out;

  xor xor_1 (xor_1_out, B1, CIN);
  xor xor_2 (xor_2_out, B2, CIN);
  Adder #(.width(1)) adder_1 (.a(A1), .b(xor_1_out), .out(S2_S1[0]), .cin(CIN), .cout(adder_1_cout));
  Adder #(.width(1)) adder_2 (.a(A2), .b(xor_2_out), .out(S2_S1[1]), .cin(adder_1_cout), .cout(COUT));

  assign A2_A1 = {A2, A1};
  assign B2_B1 = {B2, B1};

  // Notes on the sheet:
  //   Fig: 2-bit Adder-Subtractor
endmodule
