// Logisim project 4-bit Adder-Subtractor.circ as structural Verilog: 1 circuit, main circuit main
module main (
  input  CIN,
  input  A1,
  input  B1,
  input  A2,
  input  B2,
  input  A3,
  input  B3,
  input  A4,
  input  B4,
  output S1,
  output S2,
  output S3,
  output S4,
  output COUT
);

  wire adder_1_cout, adder_2_cout, adder_3_cout, xor_1_out, xor_2_out, xor_3_out, xor_4_out;

  xor xor_1 (xor_1_out, B1, CIN);
  xor xor_2 (xor_2_out, B2, CIN);
  xor xor_3 (xor_3_out, B3, CIN);
  xor xor_4 (xor_4_out, B4, CIN);
  Adder #(.width(1)) adder_1 (.a(A1), .b(xor_1_out), .out(S1), .cin(CIN), .cout(adder_1_cout));
  Adder #(.width(1)) adder_2 (.a(A2), .b(xor_2_out), .out(S2), .cin(adder_1_cout), .cout(adder_2_cout));
  Adder #(.width(1)) adder_3 (.a(A3), .b(xor_3_out), .out(S3), .cin(adder_2_cout), .cout(adder_3_cout));
  Adder #(.width(1)) adder_4 (.a(A4), .b(xor_4_out), .out(S4), .cin(adder_3_cout), .cout(COUT));

  // Notes on the sheet:
  //   Fig: 4-bit Adder-Subtractor
endmodule
