// Logisim project IC - 4-bit Adder-Subtractor - IC 74283 using Logisim Adder.circ as structural Verilog: 3 circuits, main circuit main
module main (
  input  A4,
  input  A3,
  input  A2,
  input  A1,
  input  B4,
  input  B3,
  input  B2,
  input  B1,
  input  M,
  output Cout,
  output S4,
  output S3,
  output S2,
  output S1
);

  wire ic_7486_1_y1, ic_7486_1_y2, ic_7486_1_y3, ic_7486_1_y4;

  IC_7486 ic_7486_1 (
    .A1(B1), .B1(M), .A2(M), .B2(B2), .A3(B3), .B3(M), .A4(B4), .B4(M), .Y1(ic_7486_1_y1), .Y2(ic_7486_1_y2),
    .Y3(ic_7486_1_y3), .Y4(ic_7486_1_y4));
  IC_74283_ADD ic_74283_add_1 (
    .A1(A1), .A2(A2), .A3(A3), .A4(A4), .S2(S2), .B1(ic_7486_1_y1), .B2(ic_7486_1_y2), .S3(S3),
    .B3(ic_7486_1_y3), .B4(ic_7486_1_y4), .S4(S4), .CIN(M), .S1(S1), .COUT(Cout));

  // Notes on the sheet:
  //   Fig: 4-bit Adder Subtractor
endmodule

module IC_7486 (
  input  A1,
  input  A2,
  input  A3,
  input  A4,
  input  B1,
  input  B2,
  input  B3,
  input  B4,
  output Y1,
  output Y2,
  output Y3,
  output Y4
);

  xor xor_1 (Y1, A1, B1);
  xor xor_2 (Y2, A2, B2);
  xor xor_3 (Y3, A3, B3);
  xor xor_4 (Y4, A4, B4);
endmodule

module IC_74283_ADD (
  input  CIN,
  input  A1,
  input  B1,
  input  A2,
  input  B2,
  input  A3,
  input  B3,
  input  A4,
  input  B4,
  output S1,
  output S2,
  output S3,
  output S4,
  output COUT
);

  wire adder_1_cout, adder_2_cout, adder_3_cout;

  Adder #(.width(1)) adder_1 (.a(A1), .b(B1), .out(S1), .cin(CIN), .cout(adder_1_cout));
  Adder #(.width(1)) adder_2 (.a(A2), .b(B2), .out(S2), .cin(adder_1_cout), .cout(adder_2_cout));
  Adder #(.width(1)) adder_3 (.a(A3), .b(B3), .out(S3), .cin(adder_2_cout), .cout(adder_3_cout));
  Adder #(.width(1)) adder_4 (.a(A4), .b(B4), .out(S4), .cin(adder_3_cout), .cout(COUT));
endmodule
