// Logisim project IC - BCD Adder - IC 74283 using Logisim Adder.circ as structural Verilog: 4 circuits, main circuit main
module main (
  input  [7:0] A4_A3_A2_A1_B4_B3_B2_B1,
  input  CIN,
  input  CIN_2,
  output BCD_Carry,
  output COUT,
  output [3:0] S4_S3_S2_S1
);

  wire ic_7408_and_1_y3, ic_7408_and_1_y4, ic_7432_or_1_y3, ic_74283_add_1_cout, ic_74283_add_1_s1,
       ic_74283_add_1_s2, ic_74283_add_1_s3, ic_74283_add_1_s4;

  IC_7432_OR ic_7432_or_1 (
    .A3(ic_7408_and_1_y4), .B3(ic_7408_and_1_y3), .A4(ic_74283_add_1_cout), .B4(ic_7432_or_1_y3),
    .Y3(ic_7432_or_1_y3), .Y4(BCD_Carry));  // open: A1, B1, A2, B2, Y1, Y2
  IC_7408_AND ic_7408_and_1 (
    .A3(ic_74283_add_1_s4), .B3(ic_74283_add_1_s2), .A4(ic_74283_add_1_s3), .B4(ic_74283_add_1_s4),
    .Y3(ic_7408_and_1_y3), .Y4(ic_7408_and_1_y4));  // open: A1, B1, A2, B2, Y1, Y2
  IC_74283_ADD ic_74283_add_1 (
    .CIN(CIN), .A1(A4_A3_A2_A1_B4_B3_B2_B1[4]), .B1(A4_A3_A2_A1_B4_B3_B2_B1[0]),
    .A2(A4_A3_A2_A1_B4_B3_B2_B1[5]), .B2(A4_A3_A2_A1_B4_B3_B2_B1[1]), .A3(A4_A3_A2_A1_B4_B3_B2_B1[6]),
    .B3(A4_A3_A2_A1_B4_B3_B2_B1[2]), .A4(A4_A3_A2_A1_B4_B3_B2_B1[7]), .B4(A4_A3_A2_A1_B4_B3_B2_B1[3]),
    .S1(ic_74283_add_1_s1), .S2(ic_74283_add_1_s2), .S3(ic_74283_add_1_s3), .S4(ic_74283_add_1_s4),
    .COUT(ic_74283_add_1_cout));
  IC_74283_ADD ic_74283_add_2 (
    .CIN(CIN_2), .A1(1'b0), .B1(ic_74283_add_1_s1), .A2(BCD_Carry), .B2(ic_74283_add_1_s2), .A3(BCD_Carry),
    .B3(ic_74283_add_1_s3), .A4(1'b0), .B4(ic_74283_add_1_s4), .S1(S4_S3_S2_S1[0]), .S2(S4_S3_S2_S1[1]),
    .S3(S4_S3_S2_S1[2]), .S4(S4_S3_S2_S1[3]), .COUT(COUT));

  // Notes on the sheet:
  //   Fig: BCD Adder
endmodule

module IC_7408_AND (
  input  A1,
  input  A2,
  input  A3,
  input  A4,
  input  B1,
  input  B2,
  input  B3,
  input  B4,
  output Y1,
  output Y2,
  output Y3,
  output Y4
);

  and and_1 (Y1, A1, B1);
  and and_2 (Y2, A2, B2);
  and and_3 (Y3, A3, B3);
  and and_4 (Y4, A4, B4);
endmodule

module IC_7432_OR (
  input  A1,
  input  A2,
  input  A3,
  input  A4,
  input  B1,
  input  B2,
  input  B3,
  input  B4,
  output Y1,
  output Y2,
  output Y3,
  output Y4
);

  or or_1 (Y1, A1, B1);
  or or_2 (Y2, A2, B2);
  or or_3 (Y3, A3, B3);
  or or_4 (Y4, A4, B4);
endmodule

module IC_74283_ADD (
  input  CIN,
  input  A1,
  input  B1,
  input  A2,
  input  B2,
  input  A3,
  input  B3,
  input  A4,
  input  B4,
  output S1,
  output S2,
  output S3,
  output S4,
  output COUT
);

  wire adder_1_cout, adder_2_cout, adder_3_cout;

  Adder #(.width(1)) adder_1 (.a(A1), .b(B1), .out(S1), .cin(CIN), .cout(adder_1_cout));
  Adder #(.width(1)) adder_2 (.a(A2), .b(B2), .out(S2), .cin(adder_1_cout), .cout(adder_2_cout));
  Adder #(.width(1)) adder_3 (.a(A3), .b(B3), .out(S3), .cin(adder_2_cout), .cout(adder_3_cout));
  Adder #(.width(1)) adder_4 (.a(A4), .b(B4), .out(S4), .cin(adder_3_cout), .cout(COUT));
endmodule
