// Logisim project IC - BCD Adder - Original IC 74283 ADD.circ as structural Verilog: 4 circuits, main circuit main
module main (
  input  [7:0] A4_A3_A2_A1_B4_B3_B2_B1,
  input  CIN,
  input  CIN_2,
  output BCD_Carry,
  output COUT,
  output [3:0] S4_S3_S2_S1
);

  wire ic_7408_and_1_y3, ic_7408_and_1_y4, ic_7432_or_1_y3, ic_74283_add_1_cout, ic_74283_add_1_s1,
       ic_74283_add_1_s2, ic_74283_add_1_s3, ic_74283_add_1_s4;

  IC_7432_OR ic_7432_or_1 (
    .A3(ic_7408_and_1_y4), .B3(ic_7408_and_1_y3), .A4(ic_74283_add_1_cout), .B4(ic_7432_or_1_y3),
    .Y3(ic_7432_or_1_y3), .Y4(BCD_Carry));  // open: A1, B1, A2, B2, Y1, Y2
  IC_7408_AND ic_7408_and_1 (
    .A3(ic_74283_add_1_s4), .B3(ic_74283_add_1_s2), .A4(ic_74283_add_1_s3), .B4(ic_74283_add_1_s4),
    .Y3(ic_7408_and_1_y3), .Y4(ic_7408_and_1_y4));  // open: A1, B1, A2, B2, Y1, Y2
  IC_74283_ADD ic_74283_add_1 (
    .CIN(CIN), .A1(A4_A3_A2_A1_B4_B3_B2_B1[4]), .B1(A4_A3_A2_A1_B4_B3_B2_B1[0]),
    .A2(A4_A3_A2_A1_B4_B3_B2_B1[5]), .B2(A4_A3_A2_A1_B4_B3_B2_B1[1]), .A3(A4_A3_A2_A1_B4_B3_B2_B1[6]),
    .B3(A4_A3_A2_A1_B4_B3_B2_B1[2]), .A4(A4_A3_A2_A1_B4_B3_B2_B1[7]), .B4(A4_A3_A2_A1_B4_B3_B2_B1[3]),
    .S1(ic_74283_add_1_s1), .S2(ic_74283_add_1_s2), .S3(ic_74283_add_1_s3), .S4(ic_74283_add_1_s4),
    .COUT(ic_74283_add_1_cout));
  IC_74283_ADD ic_74283_add_2 (
    .CIN(CIN_2), .A1(1'b0), .B1(ic_74283_add_1_s1), .A2(BCD_Carry), .B2(ic_74283_add_1_s2), .A3(BCD_Carry),
    .B3(ic_74283_add_1_s3), .A4(1'b0), .B4(ic_74283_add_1_s4), .S1(S4_S3_S2_S1[0]), .S2(S4_S3_S2_S1[1]),
    .S3(S4_S3_S2_S1[2]), .S4(S4_S3_S2_S1[3]), .COUT(COUT));

  // Notes on the sheet:
  //   Fig: BCD Adder
endmodule

module IC_7408_AND (
  input  A1,
  input  A2,
  input  A3,
  input  A4,
  input  B1,
  input  B2,
  input  B3,
  input  B4,
  output Y1,
  output Y2,
  output Y3,
  output Y4
);

  and and_1 (Y1, A1, B1);
  and and_2 (Y2, A2, B2);
  and and_3 (Y3, A3, B3);
  and and_4 (Y4, A4, B4);
endmodule

module IC_7432_OR (
  input  A1,
  input  A2,
  input  A3,
  input  A4,
  input  B1,
  input  B2,
  input  B3,
  input  B4,
  output Y1,
  output Y2,
  output Y3,
  output Y4
);

  or or_1 (Y1, A1, B1);
  or or_2 (Y2, A2, B2);
  or or_3 (Y3, A3, B3);
  or or_4 (Y4, A4, B4);
endmodule

module IC_74283_ADD (
  input  A1,
  input  A2,
  input  A3,
  input  A4,
  input  B1,
  input  B2,
  input  B3,
  input  B4,
  input  CIN,
  output S1,
  output S2,
  output S3,
  output S4,
  output COUT
);

  wire and_1_out, and_2_out, and_3_out, and_4_out, and_5_out, and_6_out, and_7_out, and_8_out, and_9_out,
       and_10_out, and_11_out, and_12_out, and_13_out, and_14_out, nand_1_out, nand_2_out, nand_3_out,
       nand_4_out, nor_1_out, nor_2_out, nor_3_out, nor_4_out, nor_5_out, nor_6_out, nor_7_out, not_1_out,
       not_2_out, not_3_out, not_4_out, not_5_out, not_6_out;

  not not_1 (not_1_out, CIN);
  nor nor_1 (nor_1_out, A1, B1);
  nand nand_1 (nand_1_out, A1, B1);
  nor nor_2 (nor_2_out, A2, B2);
  nand nand_2 (nand_2_out, A2, B2);
  nor nor_3 (nor_3_out, A3, B3);
  nand nand_3 (nand_3_out, A3, B3);
  nor nor_4 (nor_4_out, A4, B4);
  nand nand_4 (nand_4_out, A4, B4);
  not not_2 (not_2_out, not_1_out);
  not not_3 (not_3_out, nor_1_out);
  and and_1 (and_1_out, not_1_out, nand_1_out);
  not not_4 (not_4_out, nor_2_out);
  and and_2 (and_2_out, not_1_out, nand_1_out, nand_2_out);
  and and_3 (and_3_out, nand_2_out, nor_1_out);
  not not_5 (not_5_out, nor_3_out);
  and and_4 (and_4_out, not_1_out, nand_1_out, nand_2_out, nand_3_out);
  and and_5 (and_5_out, nand_2_out, nand_3_out, nor_1_out);
  and and_6 (and_6_out, nand_3_out, nor_2_out);
  not not_6 (not_6_out, nor_4_out);
  and and_7 (and_7_out, not_1_out, nand_1_out, nand_2_out, nand_3_out, nand_4_out);
  and and_8 (and_8_out, nand_2_out, nand_3_out, nand_4_out, nor_1_out);
  and and_9 (and_9_out, nand_3_out, nand_4_out, nor_2_out);
  and and_10 (and_10_out, nand_4_out, nor_3_out);
  and and_11 (and_11_out, not_3_out, nand_1_out);
  nor nor_5 (nor_5_out, and_1_out, nor_1_out);
  and and_12 (and_12_out, not_4_out, nand_2_out);
  nor nor_6 (nor_6_out, and_2_out, and_3_out, nor_2_out);
  and and_13 (and_13_out, not_5_out, nand_3_out);
  nor nor_7 (nor_7_out, and_4_out, and_5_out, and_6_out, nor_3_out);
  and and_14 (and_14_out, not_6_out, nand_4_out);
  nor nor_8 (COUT, and_7_out, and_8_out, and_9_out, and_10_out, nor_4_out);
  xor xor_1 (S1, not_2_out, and_11_out);
  xor xor_2 (S2, nor_5_out, and_12_out);
  xor xor_3 (S3, nor_6_out, and_13_out);
  xor xor_4 (S4, nor_7_out, and_14_out);
endmodule
