// Logisim project BCD to Seven Segment Decoder.circ as structural Verilog: 1 circuit, main circuit main
module main (
  input  D,
  input  C,
  input  B,
  input  A
);

  wire a_out, and_1_out, and_2_out, and_3_out, and_4_out, and_5_out, and_6_out, and_7_out, and_8_out,
       and_9_out, and_10_out, and_11_out, and_12_out, and_13_out, and_14_out, and_15_out, and_16_out, b_out,
       c_out, d_out, e_out, f_out, g_out, not_1_out, not_2_out, not_3_out;

  not not_1 (not_1_out, A);
  not not_2 (not_2_out, B);
  not not_3 (not_3_out, C);
  and and_1 (and_1_out, A, C);
  and and_2 (and_2_out, not_1_out, not_3_out);
  and and_3 (and_3_out, A, B);
  and and_4 (and_4_out, not_1_out, not_2_out);
  and and_5 (and_5_out, not_1_out, B);
  and and_6 (and_6_out, not_1_out, not_3_out);
  and and_7 (and_7_out, B, not_3_out);
  and and_8 (and_8_out, A, not_2_out, C);
  and and_9 (and_9_out, not_1_out, not_3_out);
  and and_10 (and_10_out, not_1_out, B);
  and and_11 (and_11_out, not_1_out, not_2_out);
  and and_12 (and_12_out, not_1_out, C);
  and and_13 (and_13_out, not_2_out, C);
  and and_14 (and_14_out, not_1_out, C);
  and and_15 (and_15_out, B, not_3_out);
  and and_16 (and_16_out, not_2_out, C);
  or u_a (a_out, B, D, and_1_out, and_2_out);
  or u_b (b_out, not_3_out, and_3_out, and_4_out);
  or u_c (c_out, A, not_2_out, C);
  or u_d (d_out, D, and_5_out, and_6_out, and_7_out, and_8_out);
  or e (e_out, and_9_out, and_10_out);
  or f (f_out, D, and_11_out, and_12_out, and_13_out);
  or g (g_out, D, and_14_out, and_15_out, and_16_out);
  _7_Segment_Display u_7_segment_display_1 (
    .g(g_out), .f(f_out), .a(a_out), .b(b_out), .e(e_out), .d(d_out), .c(c_out));  // open: dp

  // Notes on the sheet:
  //   Fig: BCD to Seven Segment Decoder
  //   c=A+B'+C
  //   e=A'C'+A'B
  //   f=D+A'B'+A'C+B'C
  //   g=D+A'C+BC'+B'C
  //   a=B+D+AC+A'C'
  //   b=C'+AB+A'B'
  //   d=D+A'B+A'C'+BC'+AB'C
endmodule
