// Logisim project F(A, B, C) = Minterms (0, 1, 5, 7) 4-To-1 Multiplexer.circ as structural Verilog: 1 circuit, main circuit main
module main (
  input  Enable,
  input  A,
  input  B,
  input  C,
  output F
);

  wire and_1_out, and_2_out, and_3_out, and_4_out, not_1_out, not_2_out, or_1_out, or_2_out;

  not not_1 (not_1_out, A);
  not not_2 (not_2_out, B);
  and and_1 (and_1_out, Enable, 1'b1, not_1_out, not_2_out);
  and and_2 (and_2_out, Enable, 1'b0, not_1_out, B);
  and and_3 (and_3_out, Enable, C, A, not_2_out);
  and and_4 (and_4_out, Enable, C, A, B);
  or or_1 (or_1_out, and_1_out, and_2_out);
  or or_2 (or_2_out, and_3_out, and_4_out);
  or or_3 (F, or_1_out, or_2_out);

  // Notes on the sheet:
  //   Fig: F(A, B, C) = Σ (0, 1, 5, 7) 4:1 Multiplexer
endmodule
