// Logisim project F(A, B, C, D) = Minterms (1, 2, 4, 5, 10, 12, 13) 8-To-1 Multiplexer.circ as structural Verilog: 1 circuit, main circuit main
module main (
  input  [2:0] A__B_C,
  input  D,
  output F
);

  Multiplexer #(.select(3), .enable("false")) multiplexer_1 (
    .in0(1'b1), .in1(D), .in2(D), .in3(1'b0), .in4(1'b1), .in5(1'b0), .in6(1'b0), .in7(1'b1), .out(F),
    .sel(A__B_C));

  // Notes on the sheet:
  //   Fig: F(A, B, C, D) = Σ (1, 2, 4, 5, 10, 12, 13) 8:1 Multiplexer
endmodule
