// Logisim project 1-bit Full Adder using Decoder.circ as structural Verilog: 1 circuit, main circuit main
module main (
  input  A,
  input  B,
  input  Cin,
  output Sum,
  output Carry
);

  wire decoder_1_out1, decoder_1_out2, decoder_1_out3, decoder_1_out4, decoder_1_out5, decoder_1_out6,
       decoder_1_out7;

  Decoder #(.select(3), .enable("false")) decoder_1 (
    .out1(decoder_1_out1), .out2(decoder_1_out2), .out3(decoder_1_out3), .out4(decoder_1_out4),
    .out5(decoder_1_out5), .out6(decoder_1_out6), .out7(decoder_1_out7), .sel({A, B, Cin}));  // open: out0
  or \u_Σ_1_2_4_7  (Sum, decoder_1_out1, decoder_1_out2, decoder_1_out4, decoder_1_out7);
  or \u_Σ_3_5_6_7  (Carry, decoder_1_out3, decoder_1_out5, decoder_1_out6, decoder_1_out7);

  // Notes on the sheet:
  //   Fig: 1-bit Full Adder using Decoder
endmodule
