// Logisim project 3-To-8 Line Decoder (Active Low).circ as structural Verilog: 1 circuit, main circuit main
module main (
  input  [2:0] in_1,
  output out_2,
  output out_3,
  output out_4,
  output out_5,
  output out_6,
  output out_7,
  output out_8,
  output out_9
);

  wire decoder_1_out0, decoder_1_out1, decoder_1_out2, decoder_1_out3, decoder_1_out4, decoder_1_out5,
       decoder_1_out6, decoder_1_out7;

  not not_1 (out_2, decoder_1_out0);
  Decoder #(.select(3), .enable("false")) decoder_1 (
    .out0(decoder_1_out0), .out1(decoder_1_out1), .out2(decoder_1_out2), .out3(decoder_1_out3),
    .out4(decoder_1_out4), .out5(decoder_1_out5), .out6(decoder_1_out6), .out7(decoder_1_out7), .sel(in_1));
  not not_2 (out_3, decoder_1_out1);
  not not_3 (out_4, decoder_1_out2);
  not not_4 (out_5, decoder_1_out3);
  not not_5 (out_6, decoder_1_out4);
  not not_6 (out_7, decoder_1_out5);
  not not_7 (out_8, decoder_1_out6);
  not not_8 (out_9, decoder_1_out7);

  // Notes on the sheet:
  //   Fig: 3-To-8 Line Decoder (Active Low)
endmodule
